# Fritzing sketch Four digit (saved by Fritzing 0.9.3b)
breadboards: 1

parts:
  7_Segment_4_Digit_Display1 = 7-SEGMENT-4DIGIT common anode [part_number="5461BS - 5462BS" package=7-segment-4digit-anode]
  Part1 = Arduino Uno (Rev3)
  R1 = Resistor [tolerance=±5% resistance=220 package=THT]
  R2 = Resistor [tolerance=±5% resistance=220 package=THT]
  R3 = Resistor [tolerance=±5% resistance=220 package=THT]
  R4 = Resistor [tolerance=±5% resistance=220 package=THT]
  U1 = 74HC595 [package="DIP16 [THT]"]
  LED1 = LED - 5mm [color="Red (633nm)" package="5 mm [THT]"]
  R5 = Resistor [tolerance=±5% resistance=220 package=THT]
  R6 = Photocell (LDR) [package=THT]
  R7 = Resistor [tolerance=±5% resistance=1k package=THT]
  R8 = Resistor [tolerance=±5% resistance=220 package=THT]
  R9 = Resistor [tolerance=±5% resistance=220 package=THT]
  R10 = Resistor [tolerance=±5% resistance=220 package=THT]
  LED2 = RGB LED (com. cathode, rgb) [package="5 mm [THT]"]
  LED3 = LED - 5mm [color="Red (633nm)" package="5 mm [THT]"]
  LED4 = LED - 5mm [color="Green (560nm)" package="5 mm [THT]"]
  LED5 = LED - 5mm [color="Blue (470nm)" package="5 mm [THT]"]
  S1 = Pushbutton [package="[THT]"]
  S2 = Pushbutton [package="[THT]"]

nets:
  N1: 7_Segment_4_Digit_Display1.pin_1, U1.Q4
  N2: 7_Segment_4_Digit_Display1.pin_2, U1.Q3
  N3: 7_Segment_4_Digit_Display1.pin_3, U1.Q7
  N4: 7_Segment_4_Digit_Display1.pin_4, U1.Q2
  N5: 7_Segment_4_Digit_Display1.pin_5, U1.Q6
  N6: 7_Segment_4_Digit_Display1.pin_6, R1.Pin_1
  N7: 7_Segment_4_Digit_Display1.pin_7, U1.Q1
  N8: 7_Segment_4_Digit_Display1.pin_8, R2.Pin_1
  N9: 7_Segment_4_Digit_Display1.pin_9, R3.Pin_1
  N10: 7_Segment_4_Digit_Display1.pin_10, U1.Q5
  N11: 7_Segment_4_Digit_Display1.pin_11, U1.Q0
  N12: 7_Segment_4_Digit_Display1.pin_12, R4.Pin_1
  N13: Part1.A0, R6.pin_0
  N14: Part1.A1, R8.Pin_0
  N15: Part1.D8, U1.DS
  N16: Part1.D9_PWM, U1.ST_CP
  N17: Part1.D10_PWM/SS, U1.SH_CP
  N18: Part1.D11_PWM/MOSI, R4.Pin_0
  N19: Part1.D12/MISO, R3.Pin_0
  N20: Part1.D2, S1.Pin_3, S1.Pin_4
  N21: Part1.D3_PWM, S2.Pin_3, S2.Pin_4
  N22: Part1.D4, R2.Pin_0
  N23: Part1.D5_PWM, R9.Pin_0
  N24: Part1.D6_PWM, R10.Pin_0
  N25: Part1.D7, R1.Pin_0
  5V: Part1.5V, U1.MR, U1.VCC, LED1.anode, R6.pin_1, R7.Pin_0
  GND: Part1.GND, U1.GND, R5.Pin_1, R7.Pin_1, LED2.common_cathode, LED3.cathode, LED4.cathode, LED5.cathode, S1.Pin_1, S1.Pin_2, S2.Pin_1, S2.Pin_2
  N26: LED1.cathode, R5.Pin_0
  N27: R8.Pin_1, LED2.blue_anode, LED5.anode
  N28: R9.Pin_1, LED2.green_anode, LED4.anode
  N29: R10.Pin_1, LED2.red_anode, LED3.anode

custom parts:
  7-SEGMENT-4DIGIT common anode: A 7 Segment 4 Digit common anode display, with decimal points
